# Fritzing sketch ESP12_DHT11 (saved by Fritzing 0.9.3b)
breadboards: 1

parts:
  U1 = ESP8266 NodeMCU LoLin module
  DHT1 = DHT11 Humitidy and Temperature Sensor

nets:
  N1: U1.D2, DHT1.DATA
  3V3: U1.3V3, DHT1.VDD
  GND: U1.GND, DHT1.GND

custom parts:
  ESP8266 NodeMCU LoLin module: ESP8266 based NodeMCU
  DHT11 Humitidy and Temperature Sensor: DHT11 Humidity and Temperature Sensor
